// Logisim project MIPS Datapath (16-bits).circ as structural Verilog: 9 circuits, main circuit single_cycle_datapath
module single_cycle_datapath (
  input  enable,
  output Zero
);

  wire clock_1_out, main_cu_1_alusrc, main_cu_1_memread, main_cu_1_memtoreg, main_cu_1_memwrite,
       main_cu_1_regdst, main_cu_1_regwrite;
  wire [1:0] main_cu_1_aluop0;
  wire [2:0] alu_cu_1_aluoperation, multiplexer_1_out;
  wire [15:0] alu_1_alu_result, mem_1_readdata, multiplexer_2_out, multiplexer_3_out, reg_file_1_read_data1,
       reg_file_1_read_data2;
  wire [31:0] if_1_out_3;

  // Probe on reg_file_1_read_data2
  // Probe on reg_file_1_read_data1
  Clock clock_1 (.out(clock_1_out));
  IF if_1 (.clock(clock_1_out), .enable(enable), .out_3(if_1_out_3));
  // Probe on if_1_out_3
  // Probe on if_1_out_3[23:21]
  // Probe on if_1_out_3[18:16]
  Main_CU main_cu_1 (
    .op(if_1_out_3[31:26]), .RegWrite(main_cu_1_regwrite), .RegDst(main_cu_1_regdst),
    .ALUsrc(main_cu_1_alusrc), .ALUop1(main_cu_1_aluop0[1]), .ALUop0(main_cu_1_aluop0[0]),
    .MemRead(main_cu_1_memread), .MemWrite(main_cu_1_memwrite), .MemtoReg(main_cu_1_memtoreg));  // open: Branch, Jump
  Multiplexer #(.width(3), .enable("false")) multiplexer_1 (
    .in0(if_1_out_3[18:16]), .in1(if_1_out_3[13:11]), .out(multiplexer_1_out), .sel(main_cu_1_regdst));
  // Probe on multiplexer_1_out
  // Probe on multiplexer_3_out
  reg_file reg_file_1 (
    .Read_Reg1(if_1_out_3[23:21]), .Read_Reg2(if_1_out_3[18:16]), .write(main_cu_1_regwrite),
    .clock(clock_1_out), .writeRegister(multiplexer_1_out), .Writedata(multiplexer_3_out),
    .Read_Data1(reg_file_1_read_data1), .Read_Data2(reg_file_1_read_data2));
  Multiplexer #(.width(16), .enable("false")) multiplexer_2 (
    .in0(reg_file_1_read_data2), .in1(if_1_out_3[15:0]), .out(multiplexer_2_out), .sel(main_cu_1_alusrc));
  ALU alu_1 (
    .src1(reg_file_1_read_data1), .src2(multiplexer_2_out), .ALUoperation(alu_cu_1_aluoperation),
    .ALU_Result(alu_1_alu_result), .Zero_Flag(Zero));  // open: SLT_Result
  ALU_CU alu_cu_1 (.Function_Field(if_1_out_3[5:0]), .ALUop(main_cu_1_aluop0), .ALUoperation(alu_cu_1_aluoperation));
  // Probe on alu_1_alu_result
  mem mem_1 (
    .address(alu_1_alu_result), .writedata(reg_file_1_read_data2), .memwrite(main_cu_1_memwrite),
    .clock(main_cu_1_memread), .memread(clock_1_out), .readdata(mem_1_readdata));
  Multiplexer #(.width(16), .enable("false")) multiplexer_3 (
    .in0(mem_1_readdata), .in1(alu_1_alu_result), .out(multiplexer_3_out), .sel(main_cu_1_memtoreg));
  // Probe on multiplexer_3_out

  // Notes on the sheet:
  //   op code (26-31)
  //   Function (0-5)
endmodule

module IF (
  input  clock,
  input  enable,
  output [31:0] out_3
);

  wire [23:0] adder_1_out;
  wire [31:0] PC_q;
  wire [31:24] adder_1_out_2;

  RAM #(.addrWidth(24), .dataWidth(32)) ram_1 (
    .addr(adder_1_out), .data(out_3), .clk(clock), .ld(enable));  // open: sel, clr
  Register #(.width(32)) PC (.D({adder_1_out_2, adder_1_out}), .Q(PC_q), .clk(clock));  // open: en, clr
  Adder #(.width(32)) adder_1 (.a(PC_q), .b(32'h1), .out({adder_1_out_2, adder_1_out}));  // open: cin, cout

  // Notes on the sheet:
  //   Instruction Memory
endmodule

module ALU (
  input  [15:0] src1,
  input  [15:0] src2,
  input  [2:0] ALUoperation,
  output [15:0] ALU_Result,
  output SLT_Result,
  output Zero_Flag
);

  wire [15:0] adder_1_out, and_1_out, or_1_out, subtractor_1_out, subtractor_2_out;

  assign and_1_out = src1 & src2;  // AND_Gate and_1, 16 bits wide
  assign or_1_out = src1 | src2;  // OR_Gate or_1, 16 bits wide
  Adder #(.width(16)) adder_1 (.a(src1), .b(src2), .out(adder_1_out));  // open: cin, cout
  Subtractor #(.width(16)) subtractor_1 (.a(src1), .b(src2), .out(subtractor_1_out));  // open: bin, bout
  Subtractor #(.width(16)) subtractor_2 (.a(src1), .b(src2), .out(subtractor_2_out));  // open: bin, bout
  Multiplexer #(.select(3), .width(16), .enable("false")) multiplexer_1 (
    .in0(and_1_out), .in1(or_1_out), .in2(adder_1_out), .in6(subtractor_1_out), .out(ALU_Result),
    .sel(ALUoperation));  // open: in3, in4, in5, in7
  and and_2 (SLT_Result, ALU_Result[0], 1'b1);
  nor nor_1 (Zero_Flag, ALU_Result[0], ALU_Result[1], ALU_Result[2], ALU_Result[3], ALU_Result[4], ALU_Result[5], ALU_Result[6], ALU_Result[7], ALU_Result[8], ALU_Result[9], ALU_Result[10], ALU_Result[11], ALU_Result[12], ALU_Result[13], ALU_Result[14], ALU_Result[15]);
endmodule

// Reg File
module reg_file (
  input  [2:0] Read_Reg1,
  input  [2:0] Read_Reg2,
  input  write,
  input  clock,
  input  [2:0] writeRegister,
  input  [15:0] Writedata,
  output [15:0] Read_Data1,
  output [15:0] Read_Data2
);

  wire and_1_out, and_2_out, and_3_out, and_4_out, and_5_out, and_6_out, and_7_out, and_8_out,
       decoder_1_out0, decoder_1_out1, decoder_1_out2, decoder_1_out3, decoder_1_out4, decoder_1_out5,
       decoder_1_out6, decoder_1_out7;
  wire [15:0] _0_q, _1_q, _2_q, _3_q, _4_q, _5_q, _6_q, _7_q;

  Decoder #(.select(3), .enable("false")) decoder_1 (
    .out0(decoder_1_out0), .out1(decoder_1_out1), .out2(decoder_1_out2), .out3(decoder_1_out3),
    .out4(decoder_1_out4), .out5(decoder_1_out5), .out6(decoder_1_out6), .out7(decoder_1_out7),
    .sel(writeRegister));
  and and_1 (and_1_out, decoder_1_out0, write);
  and and_2 (and_2_out, decoder_1_out1, write);
  and and_3 (and_3_out, decoder_1_out2, write);
  and and_4 (and_4_out, decoder_1_out3, write);
  and and_5 (and_5_out, decoder_1_out4, write);
  and and_6 (and_6_out, decoder_1_out5, write);
  and and_7 (and_7_out, decoder_1_out6, write);
  and and_8 (and_8_out, decoder_1_out7, write);
  Register #(.width(16)) _0 (.D(Writedata), .en(and_1_out), .Q(_0_q), .clk(clock));  // open: clr
  Register #(.width(16)) _1 (.D(Writedata), .en(and_2_out), .Q(_1_q), .clk(clock));  // open: clr
  Register #(.width(16)) _2 (.D(Writedata), .en(and_3_out), .Q(_2_q), .clk(clock));  // open: clr
  Register #(.width(16)) _3 (.D(Writedata), .en(and_4_out), .Q(_3_q), .clk(clock));  // open: clr
  Register #(.width(16)) _4 (.D(Writedata), .en(and_5_out), .Q(_4_q), .clk(clock));  // open: clr
  Register #(.width(16)) _5 (.D(Writedata), .en(and_6_out), .Q(_5_q), .clk(clock));  // open: clr
  Register #(.width(16)) _6 (.D(Writedata), .en(and_7_out), .Q(_6_q), .clk(clock));  // open: clr
  Register #(.width(16)) _7 (.D(Writedata), .en(and_8_out), .Q(_7_q), .clk(clock));  // open: clr
  Multiplexer #(.select(3), .width(16)) multiplexer_1 (
    .in0(_0_q), .in1(_1_q), .in2(_2_q), .in3(_3_q), .in4(_4_q), .in5(_5_q), .in6(_6_q), .in7(_7_q),
    .out(Read_Data1), .sel(Read_Reg1));  // open: en
  Multiplexer #(.select(3), .width(16)) multiplexer_2 (
    .in0(_0_q), .in1(_1_q), .in2(_2_q), .in3(_3_q), .in4(_4_q), .in5(_5_q), .in6(_6_q), .in7(_7_q),
    .out(Read_Data2), .sel(Read_Reg2));  // open: en
endmodule

// Data Mem
module mem (
  input  [15:0] address,
  input  [15:0] writedata,
  input  memwrite,
  input  clock,
  input  memread,
  output [15:0] readdata
);

  RAM #(.addrWidth(16), .dataWidth(16), .bus("separate")) ram_1 (
    .addr(address), .din(writedata), .data(readdata), .str(memwrite), .clk(clock), .ld(memread));  // open: sel, clr
endmodule

module Lab_11 (
  input  Write
);

  wire Clock_out;
  wire [15:0] alu_1_alu_result, reg_file_1_read_data1, reg_file_1_read_data2;
  wire [31:0] if_1_out_3;

  Clock Clock (.out(Clock_out));
  IF if_1 (.clock(Clock_out), .enable(1'b1), .out_3(if_1_out_3));
  // Probe on if_1_out_3
  // Probe on if_1_out_3[13:11]
  // Probe on if_1_out_3[23:21]
  // Probe on if_1_out_3[18:16]
  reg_file reg_file_1 (
    .Read_Reg1(if_1_out_3[23:21]), .Read_Reg2(if_1_out_3[18:16]), .write(Write), .clock(Clock_out),
    .writeRegister(if_1_out_3[13:11]), .Writedata(16'h5000), .Read_Data1(reg_file_1_read_data1),
    .Read_Data2(reg_file_1_read_data2));
  // Probe on alu_1_alu_result
  ALU alu_1 (
    .src1(reg_file_1_read_data1), .src2(reg_file_1_read_data2), .ALUoperation(3'b010),
    .ALU_Result(alu_1_alu_result));  // open: SLT_Result, Zero_Flag
  // Probe on alu_1_alu_result
endmodule

module Lab_13__CU (
);

  single_cycle_datapath single_cycle_datapath_1 ();  // open: enable, Zero
  Main_CU main_cu_1 ();  // open: op, RegWrite, RegDst, ALUsrc, ALUop1, ALUop0, MemRead, MemWrite, MemtoReg, Branch, Jump
endmodule

module ALU_CU (
  input  [1:0] ALUop,
  input  [5:0] Function_Field,
  output [2:0] ALUoperation
);

  wire and_1_out, or_1_out;

  or or_1 (or_1_out, Function_Field[3], Function_Field[0]);
  and and_1 (and_1_out, ALUop[1], Function_Field[1]);
  and and_2 (ALUoperation[0], ALUop[1], or_1_out);
  or or_2 (ALUoperation[2], ALUop[0], and_1_out);
  or or_3 (ALUoperation[1], ~ALUop[1], ~Function_Field[2]);  // OR_Gate
endmodule

// CU
module Main_CU (
  input  [5:0] op,
  output RegWrite,
  output RegDst,
  output ALUsrc,
  output ALUop1,
  output ALUop0,
  output MemRead,
  output MemWrite,
  output MemtoReg,
  output Branch,
  output Jump
);

  wire not_1_out, not_2_out, not_3_out, not_4_out, not_5_out, not_6_out;

  not not_1 (not_1_out, op[5]);
  not not_2 (not_2_out, op[3]);
  not not_3 (not_3_out, op[4]);
  not not_4 (not_4_out, op[2]);
  not not_5 (not_5_out, op[1]);
  not not_6 (not_6_out, op[0]);
  and R (ALUop1, not_6_out, not_5_out, not_4_out, not_2_out, not_3_out, not_1_out);
  and lw (MemRead, op[5], not_3_out, not_2_out, not_4_out, op[1], op[0]);
  and sw (MemWrite, op[5], not_3_out, op[3], not_4_out, op[1], op[0]);
  and beq (ALUop0, not_1_out, not_3_out, not_2_out, op[2], not_5_out, not_6_out);
  and j (Jump, not_1_out, not_3_out, not_2_out, not_4_out, op[1], not_6_out);
  or or_1 (RegWrite, ALUop1, MemRead);
  or or_2 (ALUsrc, MemRead, MemWrite);

  assign Branch = ALUop0;
  assign MemtoReg = MemRead;
  assign RegDst = ALUop1;

  // Notes on the sheet:
  //   op4
  //   op5
  //   op3
  //   op2
  //   op1
  //   op0
endmodule
